// Logisim project unit1_Drill5-Half-Adder.circ as structural Verilog: 1 circuit, main circuit main
module main (
  input  A,
  input  B,
  input  in_3
);

  wire and_1_out, not_1_out, xor_1_out;

  xor xor_1 (xor_1_out, A, B);
  and and_1 (and_1_out, A, B);
  // Probe on xor_1_out
  // Probe on and_1_out
  // Probe on not_1_out
  not not_1 (not_1_out, in_3);
  LED led_1 (.in(not_1_out));

  // Notes on the sheet:
  //   Sum
  //   Carry
endmodule
