// Logisim project unit1_Drill6-full-Adder.circ as structural Verilog: 1 circuit, main circuit main
module main (
  input  A,
  input  B,
  input  Cin,
  output out_4,
  output Carry
);

  wire and_1_out, and_2_out, xor_1_out;

  xor xor_1 (xor_1_out, A, B);
  xor xor_2 (out_4, xor_1_out, Cin);
  and and_1 (and_1_out, Cin, xor_1_out);
  and and_2 (and_2_out, A, B);
  or or_1 (Carry, and_1_out, and_2_out);

  // Notes on the sheet:
  //   A xor B
  //   Cin
  //   Sum = Cin xor (A xor B)
  //   Cout = AB + Cin(A xorB)
endmodule
