// Logisim project unit1_Drill7_TriState_Bus_Sharing.circ as structural Verilog: 1 circuit, main circuit main
module main (
  input  in_1,
  input  in_2,
  input  in_3,
  input  in_4,
  output out_5,
  output out_6,
  output out_7
);

  assign out_5 = in_1 ? in_3 : 1'bz;  // Controlled_Buffer controlled_buffer_1
  assign out_5 = in_2 ? in_4 : 1'bz;  // Controlled_Buffer controlled_buffer_2

  assign out_6 = out_5;
  assign out_7 = out_5;

  // Notes on the sheet:
  //   Keyboard
  //   Input
  //   Mouse
  //   Enable pins
  //   Output
endmodule
